// Digital circuit 8位加法器(合并).dig as structural Verilog
module \_8位加法器_合并  (
  input  [7:0] A,
  input  [7:0] B,
  output [7:0] SUM,
  output Carry
);

  wire \全加器_1_carry , \全加器_2_carry , \全加器_3_carry , \全加器_4_carry , \全加器_5_carry , \全加器_6_carry ,
       \半加器_1_carry ;

  \半加器  \u_半加器_1  (.A(A[0]), .B(B[0]), .SUM(SUM[0]), .Carry(\半加器_1_carry ));
  \全加器  \u_全加器_1  (.C(\半加器_1_carry ), .A(A[1]), .B(B[1]), .SUM(SUM[1]), .Carry(\全加器_1_carry ));
  \全加器  \u_全加器_2  (.C(\全加器_1_carry ), .A(A[2]), .B(B[2]), .SUM(SUM[2]), .Carry(\全加器_2_carry ));
  \全加器  \u_全加器_3  (.C(\全加器_2_carry ), .A(A[3]), .B(B[3]), .SUM(SUM[3]), .Carry(\全加器_3_carry ));
  \全加器  \u_全加器_4  (.C(\全加器_3_carry ), .A(A[4]), .B(B[4]), .SUM(SUM[4]), .Carry(\全加器_4_carry ));
  \全加器  \u_全加器_5  (.C(\全加器_4_carry ), .A(A[5]), .B(B[5]), .SUM(SUM[5]), .Carry(\全加器_5_carry ));
  \全加器  \u_全加器_6  (.C(\全加器_5_carry ), .A(A[6]), .B(B[6]), .SUM(SUM[6]), .Carry(\全加器_6_carry ));
  \全加器  \u_全加器_7  (.C(\全加器_6_carry ), .A(A[7]), .B(B[7]), .SUM(SUM[7]), .Carry(Carry));
endmodule
