// Digital circuit ALU.dig as structural Verilog
module ALU (
  input  [7:0] RegA,
  input  [7:0] RegB,
  input  OE,
  output [7:0] Dout,
  output [7:0] ALU_Result,
  output Carry_out
);

  Add #(.Bits(8)) ALU (.a(RegA), .b(RegB), .c_i(1'b0), .s(ALU_Result), .c_o(Carry_out));
  assign Dout = OE ? ALU_Result : 8'bz;  // Driver driver_1

  // Notes on the sheet:
  //   Dout: data output
  //   数据 输出
  //   ALU_Result: 算术逻辑单元 结果展示
  //   OE: output enable
  //   输出  启用
endmodule
