// Digital circuit 与门.dig as structural Verilog
module \与门  (
  input  A,
  input  B,
  output C
);

  wire relaydt_1_p4;

  // RelayDT relaydt_1: pin names not known; wires that end beside it: A, 1'b1, 1'b0, relaydt_1_p4
  // RelayDT relaydt_2: pin names not known; wires that end beside it: B, relaydt_1_p4, 1'b0, C
  PullDown pulldown_1 (.out(C));

  // Notes on the sheet:
  //   与门：两个都为高时，才为高，其他均为低。
endmodule
