// Digital circuit 半加器.dig as structural Verilog
module \半加器  (
  input  A,
  input  B,
  output SUM,
  output Carry
);

  \异或门  \u_异或门_1  (.A(A), .B(B), .C(SUM));
  \与门  \u_与门_1  (.A(A), .B(B), .C(Carry));
endmodule
