// Digital circuit 异或门.dig as structural Verilog
module \异或门  (
  input  A,
  input  B,
  output C
);

  wire relaydt_1_p4, relaydt_1_p5;

  // RelayDT relaydt_1: pin names not known; wires that end beside it: A, 1'b1, 1'b0, relaydt_1_p4, relaydt_1_p5
  // RelayDT relaydt_2: pin names not known; wires that end beside it: B, relaydt_1_p5, relaydt_1_p4, 1'b0, C
  PullDown pulldown_1 (.out(C));

  // Notes on the sheet:
  //   异或门：相同为0（低电平），不同为1（高电平）
endmodule
