// Digital circuit 或门.dig as structural Verilog
module \或门  (
  input  A,
  input  B,
  output C
);

  // RelayDT relaydt_1: pin names not known; wires that end beside it: A, 1'b1, 1'b0, C
  // RelayDT relaydt_2: pin names not known; wires that end beside it: B, 1'b1, 1'b0, C
  PullDown pulldown_1 (.out(C));

  // Notes on the sheet:
  //   或门：当全部输入低电平时，输出才为低电平，其他均为高电平。
endmodule
