// Digital circuit 16位内存控制单元.dig as structural Verilog
module \_16位内存控制单元  (
  input  Din,
  input  store,
  input  load,
  input  [3:0] Address,
  output Dout
);

  wire [7:0] lookuptable_1_out;

  LookUpTable #(.Bits(8)) lookuptable_1 (
    .in0(Address[0]), .in1(Address[1]), .in2(Address[2]), .in3(Address[3]), .out(lookuptable_1_out));
  Memory_Cell memory_cell_1 (
    .Din(Din), .store(store), .load(load), .col(lookuptable_1_out[4]), .row(lookuptable_1_out[0]), .Dout(Dout));
  Memory_Cell memory_cell_2 (
    .Din(Din), .store(store), .load(load), .col(lookuptable_1_out[4]), .row(lookuptable_1_out[1]), .Dout(Dout));
  Memory_Cell memory_cell_3 (
    .Din(Din), .store(store), .load(load), .col(lookuptable_1_out[4]), .row(lookuptable_1_out[2]), .Dout(Dout));
  Memory_Cell memory_cell_4 (
    .Din(Din), .store(store), .load(load), .col(lookuptable_1_out[4]), .row(lookuptable_1_out[3]), .Dout(Dout));
  Memory_Cell memory_cell_5 (
    .Din(Din), .store(store), .load(load), .col(lookuptable_1_out[5]), .row(lookuptable_1_out[0]), .Dout(Dout));
  Memory_Cell memory_cell_6 (
    .Din(Din), .store(store), .load(load), .col(lookuptable_1_out[5]), .row(lookuptable_1_out[1]), .Dout(Dout));
  Memory_Cell memory_cell_7 (
    .Din(Din), .store(store), .load(load), .col(lookuptable_1_out[5]), .row(lookuptable_1_out[2]), .Dout(Dout));
  Memory_Cell memory_cell_8 (
    .Din(Din), .store(store), .load(load), .col(lookuptable_1_out[5]), .row(lookuptable_1_out[3]), .Dout(Dout));
  Memory_Cell memory_cell_9 (
    .Din(Din), .store(store), .load(load), .col(lookuptable_1_out[6]), .row(lookuptable_1_out[0]), .Dout(Dout));
  Memory_Cell memory_cell_10 (
    .Din(Din), .store(store), .load(load), .col(lookuptable_1_out[6]), .row(lookuptable_1_out[1]), .Dout(Dout));
  Memory_Cell memory_cell_11 (
    .Din(Din), .store(store), .load(load), .col(lookuptable_1_out[6]), .row(lookuptable_1_out[2]), .Dout(Dout));
  Memory_Cell memory_cell_12 (
    .Din(Din), .store(store), .load(load), .col(lookuptable_1_out[6]), .row(lookuptable_1_out[3]), .Dout(Dout));
  Memory_Cell memory_cell_13 (
    .Din(Din), .store(store), .load(load), .col(lookuptable_1_out[7]), .row(lookuptable_1_out[0]), .Dout(Dout));
  Memory_Cell memory_cell_14 (
    .Din(Din), .store(store), .load(load), .col(lookuptable_1_out[7]), .row(lookuptable_1_out[1]), .Dout(Dout));
  Memory_Cell memory_cell_15 (
    .Din(Din), .store(store), .load(load), .col(lookuptable_1_out[7]), .row(lookuptable_1_out[2]), .Dout(Dout));
  Memory_Cell memory_cell_16 (
    .Din(Din), .store(store), .load(load), .col(lookuptable_1_out[7]), .row(lookuptable_1_out[3]), .Dout(Dout));

  // Notes on the sheet:
  //   contents of lookuptable_1 (hex, n*v repeats v):
  //   11,21,41,81,12,22,42,82,14,24,44,84,18,28,48,88
endmodule
