// Digital circuit 8位寄存器.dig as structural Verilog
module \_8位寄存器  (
  input  [7:0] Din,
  input  WE,
  input  OE,
  input  Clock,
  output [7:0] Dout,
  output [7:0] Stored_data
);

  Register #(.Bits(8)) register_1 (.D(Din), .C(Clock), .en(WE), .Q(Stored_data));
  assign Dout = OE ? Stored_data : 8'bz;  // Driver driver_1
endmodule
