// Digital circuit ALU.dig as structural Verilog
module ALU (
  input  [7:0] RegA,
  input  OE,
  input  [7:0] RegB,
  output Carry,
  output [7:0] Dout,
  output [7:0] ALU_Result
);

  Add #(.Bits(8)) ALU (.a(RegA), .b(RegB), .c_i(1'b0), .s(ALU_Result), .c_o(Carry));
  assign Dout = OE ? ALU_Result : 8'bz;  // Driver driver_1
endmodule
