// Digital circuit EEPROM.dig as structural Verilog
module EEPROM (
  input  [3:0] address,
  input  [7:0] Din,
  input  WE,
  input  OE,
  output [7:0] Dout
);

  wire button_1_out;

  Button button_1 (.out(button_1_out));
  EEPROMDualPort #(.AddrBits(4), .Bits(8)) eepromdualport_1 (
    .A(address), .Din(Din), .str(WE), .C(button_1_out), .ld(OE), .D(Dout));

  // Notes on the sheet:
  //   contents of eepromdualport_1 (hex, n*v repeats v):
  //   ff,ee,5,3,7*0,8,0,40,0,5a
endmodule
