// Digital circuit Memory_Cell.dig as structural Verilog
module Memory_Cell (
  input  Din,
  input  store,
  input  load,
  input  col,
  input  row,
  output Dout
);

  wire and_1_out, and_2_out, and_3_out, \锁存器_1_dout ;

  and and_1 (and_1_out, col, row);
  and and_2 (and_2_out, store, and_1_out);
  and and_3 (and_3_out, load, and_1_out);
  \锁存器  \u_锁存器_1  (.Din(Din), .WE(and_2_out), .Dout(\锁存器_1_dout ));
  assign Dout = and_3_out ? \锁存器_1_dout  : 1'bz;  // Driver driver_1
endmodule
