// Digital circuit 查找表（地址线设计）.dig as structural Verilog
module \查找表_地址线设计  (
  input  [3:0] in_1
);

  wire [7:0] lookuptable_1_out;

  LookUpTable #(.Bits(8)) lookuptable_1 (
    .in0(in_1[0]), .in1(in_1[1]), .in2(in_1[2]), .in3(in_1[3]), .out(lookuptable_1_out));
  LED led_1 (.in(lookuptable_1_out[0]));
  LED led_2 (.in(lookuptable_1_out[1]));
  LED led_3 (.in(lookuptable_1_out[2]));
  LED led_4 (.in(lookuptable_1_out[3]));
  LED led_5 (.in(lookuptable_1_out[4]));
  LED led_6 (.in(lookuptable_1_out[5]));
  LED led_7 (.in(lookuptable_1_out[6]));
  LED led_8 (.in(lookuptable_1_out[7]));

  // Notes on the sheet:
  //   contents of lookuptable_1 (hex, n*v repeats v):
  //   11,21,41,81,12,22,42,82,14,24,44,84,18,28,48,88
endmodule
