// Digital circuit 程序计数器.dig as structural Verilog
module \程序计数器  (
  input  EN,
  input  Reset,
  output [1:0] Program_Count,
  output ovf
);

  wire button_1_out;

  Button button_1 (.out(button_1_out));
  Counter #(.Bits(2)) \u_程序计数器  (.en(EN), .C(button_1_out), .clr(Reset), .out(Program_Count), .ovf(ovf));

  // Notes on the sheet:
  //   ovf: over flow
endmodule
