// Digital circuit 计算机CPU设计(手动完整版).dig as structural Verilog
module \计算机CPU设计_手动完整版  (
  input  OE,
  input  WE,
  input  OE_2,
  input  WE_2,
  input  OE_3,
  input  WE_3,
  input  OE_4,
  input  WE_4,
  input  OE_5,
  input  WE_5,
  input  OE_6,
  input  WE_6,
  input  OE_7,
  input  WE_7,
  input  OE_8,
  input  EN,
  input  OE_9,
  output [7:0] Stored_data,
  output [7:0] Stored_data_2,
  output [7:0] ALU_Result,
  output Carry,
  output [7:0] Stored_data_3,
  output [7:0] Stored_data_4,
  output [7:0] IR_data,
  output [3:0] \操作数 ,
  output [3:0] \操作码 ,
  output [3:0] Stored_data_5,
  output ovf,
  output [3:0] PC
);

  wire Clock;
  wire [3:0] \MAR_内部地址寄存器_dout ;
  wire [7:0] alu_1_dout, RegA_dout, RegB_dout;

  \_8位寄存器  RegA (.Din(alu_1_dout), .WE(WE), .OE(OE_2), .Clock(Clock), .Dout(RegA_dout), .Stored_data(Stored_data));
  \_8位寄存器  RegB (.Din(alu_1_dout), .WE(WE_2), .OE(OE_3), .Clock(Clock), .Dout(RegB_dout), .Stored_data(Stored_data_2));
  Counter #(.Bits(2)) \PC程序计数器  (.en(EN), .C(Clock), .clr(1'b0), .out(PC[1:0]), .ovf(ovf));
  ALU alu_1 (.RegA(RegA_dout), .OE(OE), .RegB(RegB_dout), .Carry(Carry), .Dout(alu_1_dout), .ALU_Result(ALU_Result));
  \_8位寄存器  \IR_指令寄存器  (
    .Din(alu_1_dout), .WE(WE_5), .OE(OE_6), .Clock(Clock), .Dout({\操作码 , \操作数 }), .Stored_data(IR_data));
  assign \操作数  = OE_9 ? {2'b00, PC[1:0]} : 4'bz;  // Driver driver_1
  Button button_1 (.out(Clock));
  \_4位寄存器  \MAR_内部地址寄存器  (
    .Din(\操作数 ), .WE(WE_6), .OE(OE_7), .Clock(Clock), .Dout(\MAR_内部地址寄存器_dout ), .Stored_data(Stored_data_5));
  \_8位寄存器  \MBR_内存缓存寄存器  (
    .Din(alu_1_dout), .WE(WE_4), .OE(OE_5), .Clock(Clock), .Dout(alu_1_dout), .Stored_data(Stored_data_4));
  \_8位寄存器  Output_Reg (
    .Din(alu_1_dout), .WE(WE_3), .OE(OE_4), .Clock(Clock), .Dout(alu_1_dout), .Stored_data(Stored_data_3));
  EEPROMDualPort #(.AddrBits(4), .Bits(8)) eepromdualport_1 (
    .A(\MAR_内部地址寄存器_dout ), .Din(alu_1_dout), .str(WE_7), .C(Clock), .ld(OE_8), .D(alu_1_dout));

  assign PC[3:2] = 2'b00;

  // Notes on the sheet:
  //   CPU内部数据总线 4bit
  //   内部数据总线 8bit
  //   CPU外部数据总线 4bit
  //   contents of eepromdualport_1 (hex, n*v repeats v):
  //   e,1f,20,3f,10*0,3,8
  //   外部数据总线 8bit
endmodule
