// Digital circuit 计算机CPU设计(手动测试版).dig as structural Verilog
module \计算机CPU设计_手动测试版  (
  input  OE,
  input  WE,
  input  OE_2,
  input  WE_2,
  input  OE_3,
  input  WE_3,
  input  OE_4,
  input  [7:0] \测试信号 ,
  input  \测试开关 ,
  output [7:0] Stored_data,
  output [7:0] Stored_data_2,
  output [7:0] ALU_Result,
  output Carry,
  output [7:0] Stored_data_3
);

  wire Clock;
  wire [7:0] alu_1_dout, RegA_dout, RegB_dout;

  \_8位寄存器  RegA (.Din(alu_1_dout), .WE(WE), .OE(OE_2), .Clock(Clock), .Dout(RegA_dout), .Stored_data(Stored_data));
  \_8位寄存器  RegB (.Din(alu_1_dout), .WE(WE_2), .OE(OE_3), .Clock(Clock), .Dout(RegB_dout), .Stored_data(Stored_data_2));
  Button button_1 (.out(Clock));
  ALU alu_1 (.RegA(RegA_dout), .OE(OE), .RegB(RegB_dout), .Carry(Carry), .Dout(alu_1_dout), .ALU_Result(ALU_Result));
  assign alu_1_dout = \测试开关  ? \测试信号  : 8'bz;  // Driver driver_1
  \_8位寄存器  Output_Reg (
    .Din(alu_1_dout), .WE(WE_3), .OE(OE_4), .Clock(Clock), .Dout(alu_1_dout), .Stored_data(Stored_data_3));

  // Notes on the sheet:
  //   内部数据总线 8bit
endmodule
