// Digital circuit 计算机CPU设计(自动完整版).dig as structural Verilog
module \计算机CPU设计_自动完整版  (
  input  \指令EN ,
  input  clk,
  output [7:0] Stored_data,
  output [7:0] Stored_data_2,
  output [7:0] ALU_Result,
  output Carry,
  output [7:0] Stored_data_3,
  output [7:0] Stored_data_4,
  output [7:0] IR_data,
  output [3:0] \操作数 ,
  output [3:0] \操作码 ,
  output [3:0] Stored_data_5,
  output ovf,
  output [3:0] PC,
  output ovf_2,
  output [3:0] \操作码_2 ,
  output [2:0] \步骤序号 
);

  wire ALU_OE, IR_OE, IR_WE, MAR_OE, MAR_WE, MBR_OE, MBR_WE, Output_Reg_OE, Output_Reg_WE, PC_EN, PC_OE,
       RegA_OE, RegA_WE, RegB_OE, RegB_WE, \计算机内存_OE , \计算机内存_WE ;
  wire [3:0] \MAR_内部地址寄存器_dout ;
  wire [7:0] alu_1_dout, RegA_dout, RegB_dout;

  Counter #(.Bits(3)) \u_指令计数器  (.en(\指令EN ), .C(clk), .clr(1'b0), .out(\步骤序号 ), .ovf(ovf_2));
  LookUpTable #(.Bits(17)) \u_指令查找表  (
    .in0(\步骤序号 [0]), .in1(\步骤序号 [1]), .in2(\步骤序号 [2]), .in3(IR_data[4]), .in4(IR_data[5]), .in5(IR_data[6]),
    .in6(IR_data[7]),
    .out({Output_Reg_OE, Output_Reg_WE, MBR_OE, MBR_WE, \计算机内存_OE , \计算机内存_WE , ALU_OE, MAR_OE, MAR_WE, RegB_OE, RegB_WE, RegA_OE, RegA_WE, IR_OE, IR_WE, PC_EN, PC_OE}));
  \_8位寄存器  RegA (
    .Din(alu_1_dout), .WE(RegA_WE), .OE(RegA_OE), .Clock(clk), .Dout(RegA_dout), .Stored_data(Stored_data));
  \_8位寄存器  RegB (
    .Din(alu_1_dout), .WE(RegB_WE), .OE(RegB_OE), .Clock(clk), .Dout(RegB_dout), .Stored_data(Stored_data_2));
  Counter #(.Bits(2)) \PC程序计数器  (.en(PC_EN), .C(clk), .clr(1'b0), .out(PC[1:0]), .ovf(ovf));
  ALU alu_1 (
    .RegA(RegA_dout), .OE(ALU_OE), .RegB(RegB_dout), .Carry(Carry), .Dout(alu_1_dout), .ALU_Result(ALU_Result));
  \_8位寄存器  \IR_指令寄存器  (
    .Din(alu_1_dout), .WE(IR_WE), .OE(IR_OE), .Clock(clk), .Dout({\操作码 , \操作数 }), .Stored_data(IR_data));
  assign \操作数  = PC_OE ? {2'b00, PC[1:0]} : 4'bz;  // Driver driver_1
  \_4位寄存器  \MAR_内部地址寄存器  (
    .Din(\操作数 ), .WE(MAR_WE), .OE(MAR_OE), .Clock(clk), .Dout(\MAR_内部地址寄存器_dout ), .Stored_data(Stored_data_5));
  \_8位寄存器  \MBR_内存缓存寄存器  (
    .Din(alu_1_dout), .WE(MBR_WE), .OE(MBR_OE), .Clock(clk), .Dout(alu_1_dout), .Stored_data(Stored_data_4));
  \_8位寄存器  Output_Reg (
    .Din(alu_1_dout), .WE(Output_Reg_WE), .OE(Output_Reg_OE), .Clock(clk), .Dout(alu_1_dout),
    .Stored_data(Stored_data_3));
  EEPROMDualPort #(.AddrBits(4), .Bits(8)) \u_计算机内存  (
    .A(\MAR_内部地址寄存器_dout ), .Din(alu_1_dout), .str(\计算机内存_WE ), .C(clk), .ld(\计算机内存_OE ), .D(alu_1_dout));

  assign PC[3:2] = 2'b00;
  assign \操作码_2  = IR_data[7:4];

  // Other names for the same wires on the sheet: Clock = clk

  // Notes on the sheet:
  //   clk: Hz: 8
  //   contents of 指令查找表 (hex, n*v repeats v):
  //   101,2,3200,4004,108,3200,4010,0,101,2,3200,4004,108,3200,4040
  //   ,0,101,2,3200,4004,84a0,0,0,0,101,2,3200,4004,12108,4a00
  //   CPU内部数据总线 4bit
  //   内部数据总线 8bit
  //   CPU外部数据总线 4bit
  //   contents of 计算机内存 (hex, n*v repeats v):
  //   e,1f,20,3f,10*0,3,ab
  //   外部数据总线 8bit
endmodule
