// Digital circuit 锁存器.dig as structural Verilog
module \锁存器  (
  input  Din,
  input  WE,
  output Dout
);

  wire and_1_out, and_2_out, not_1_out, not_2_out, or_1_out;

  not not_1 (not_1_out, Din);
  and and_1 (and_1_out, Din, WE);
  and and_2 (and_2_out, not_1_out, WE);
  or or_1 (or_1_out, Dout, and_1_out);
  not not_2 (not_2_out, and_2_out);
  and and_3 (Dout, or_1_out, not_2_out);

  // Notes on the sheet:
  //   WE: write enable
endmodule
